// Logisim project 4BitCPU.circ as structural Verilog: 3 circuits, main circuit main
module main (
  input  [3:0] in_1,
  input  WriteRam,
  input  ReadRam,
  input  [3:0] in_4,
  input  AIn,
  input  AOut,
  input  BOut,
  input  BIn
);

  wire clock_1_out;
  wire [3:0] A_out_4, ram_1_dout;

  ROM rom_1 ();  // open: addr, data
  Clock clock_1 (.out(clock_1_out));
  reg4 A (.in_1(A_out_4), .Read(AIn), .Write(AOut), .out_4(A_out_4));
  reg4 B (.in_1(A_out_4), .Read(BOut), .Write(BIn), .out_4(A_out_4));
  RAM #(.addrWidth(4), .dataWidth(4)) ram_1 (
    .addr(in_1), .we(WriteRam), .oe(ReadRam), .clk(clock_1_out), .din(in_4), .dout(ram_1_dout));
  assign A_out_4 = ReadRam ? ram_1_dout : 4'bz;  // Controlled_Buffer controlled_buffer_1
  Hex_Digit_Display hex_digit_display_1 (.value(A_out_4));  // open: dp
endmodule

module reg4 (
  input  [3:0] in_1,
  input  Read,
  input  Write,
  output [3:0] out_4
);

  wire [3:0] d_ff_1_q;

  D_Flip_Flop d_ff_1 (.D(in_1[0]), .clk(Read), .Q(d_ff_1_q[0]));  // open: Qn, preset, reset
  D_Flip_Flop d_ff_2 (.D(in_1[1]), .clk(Read), .Q(d_ff_1_q[1]));  // open: Qn, preset, reset
  D_Flip_Flop d_ff_3 (.D(in_1[2]), .clk(Read), .Q(d_ff_1_q[2]));  // open: Qn, preset, reset
  D_Flip_Flop d_ff_4 (.D(in_1[3]), .clk(Read), .Q(d_ff_1_q[3]));  // open: Qn, preset, reset
  assign out_4 = Write ? d_ff_1_q : 4'bz;  // Controlled_Buffer controlled_buffer_1

  // Notes on the sheet:
  //   DataIn
endmodule

module ALU (
  input  [3:0] in_1,
  input  [3:0] in_2,
  input  [3:0] in_3
);

  Decoder #(.select(4)) decoder_1 (
    .sel(in_1), .en(1'b1));  // open: out0, out1, out2, out3, out4, out5, out6, out7, out8, out9, out10, out11, out12, out13, out14, out15
endmodule
